// Logisim project PROJECT_Abdelrhman.circ as structural Verilog: 3 circuits, main circuit Data_Unit
module Data_Unit (
  output [15:0] out_1,
  output [15:0] out_2,
  output [7:0] out_3,
  output [7:0] out_4,
  output [15:0] ADD_res,
  output FGI_FLAG,
  output E_FLAG,
  output [15:0] CMA_res,
  output FGO_FLAG,
  output [15:0] AND_res
);

  wire AC_CLR, AC_LD, ALU_ADD, ALU_AND, ALU_CMA, ALU_EN, ALU_z, AR_INC, AR_LD, C_Out, clk, clock_1_out, D7,
       DR_INC, DR_LD, E_CLR, FGI_CLR, FGO_CLR, IR_LD, LD_DATA, LD_out, or_3_out, or_4_out, OUT_DATA, OUTR_LD,
       PC_INC, PC_LD, R, S_CLR, SW_out, W, X, Z;
  wire [2:0] S2_0;
  wire [7:0] dipswitch_1_sw8, INP_Data, INP_Res, input_output_1_leds;
  wire [10:0] adder_3_out, AR_Data, multiplexer_10_out, PC_Data;
  wire [10:8] address;
  wire [15:0] adder_2_out, bit_extender_1_out, bit_extender_2_out, bit_extender_4_out,
       controlled_buffer_1_out, ins, Ins_Data, multiplexer_1_out, multiplexer_2_out, multiplexer_3_out,
       multiplexer_4_out, multiplexer_6_out, multiplexer_7_out, multiplexer_8_out, multiplexer_9_out, res;
  wire [15:11] Data;
  wire [17:0] bit_extender_3_out, ram_1_dout;

  Clock clock_1 (.out(clock_1_out));
  Multiplexer #(.width(16)) multiplexer_1 (.in0({16{1'b0}}), .in1(out_1), .out(multiplexer_1_out), .sel(ALU_ADD));
  Multiplexer #(.width(16)) multiplexer_2 (.in0({16{1'b0}}), .in1(out_2), .out(multiplexer_2_out), .sel(ALU_ADD));
  Multiplexer #(.width(16)) multiplexer_3 (.in0({16{1'b0}}), .in1(out_1), .out(multiplexer_3_out), .sel(ALU_AND));
  Multiplexer #(.width(16)) multiplexer_4 (.in0({16{1'b0}}), .in1(out_2), .out(multiplexer_4_out), .sel(ALU_AND));
  and and_1 (clk, clock_1_out, ~S_CLR);  // AND_Gate
  assign controlled_buffer_1_out = ALU_CMA ? out_1 : 16'bz;  // Controlled_Buffer controlled_buffer_1
  Control_Unit control_unit_1 (
    .Z(Z), .FGI(FGI_FLAG), .FGO(FGO_FLAG), .ins(ins), .CLK(clk), .S2_0(S2_0), .AR_LD(AR_LD), .MEM_READ(R),
    .AR_INC(AR_INC), .X(X), .ALU_AND(ALU_AND), .ALU_ADD(ALU_ADD), .ALU_CMA(ALU_CMA), .MEM_WRITE(E_CLR),
    .E_CLR(W), .AC_CLR(AC_CLR), .PC_LD(FGO_CLR), .FGO_CLR(PC_LD), .FGI_CLR(FGI_CLR), .OUTR_LD(PC_INC),
    .S_CLR(S_CLR), .IR_LD(OUTR_LD), .DR_LD(IR_LD), .AC_LD(DR_LD), .DR_INC(DR_INC), .D7(AC_LD), .PC_INC(D7));
  Adder #(.width(16)) adder_1 (.a(multiplexer_1_out), .b(multiplexer_2_out), .out(ADD_res), .cout(C_Out));  // open: cin
  Negator #(.width(16)) negator_1 (.in(controlled_buffer_1_out), .out(CMA_res));
  assign AND_res = multiplexer_3_out & multiplexer_4_out;  // AND_Gate and_2, 16 bits wide
  assign res = ALU_ADD ? ADD_res : 16'bz;  // Controlled_Buffer controlled_buffer_2
  assign res = ALU_CMA ? CMA_res : 16'bz;  // Controlled_Buffer controlled_buffer_3
  assign res = ALU_AND ? AND_res : 16'bz;  // Controlled_Buffer controlled_buffer_4
  assign bit_extender_1_out = {{5{1'b0}}, PC_Data};  // Bit_Extender bit_extender_1
  assign bit_extender_2_out = {{5{1'b0}}, AR_Data};  // Bit_Extender bit_extender_2
  Counter #(.max('h7ff), .width(11)) counter_1 (
    .load(PC_LD), .up(1'b1), .count(PC_INC), .clk(clk), .D({address, out_3}), .Q(PC_Data));  // open: clr, carry
  Multiplexer #(.select(3), .width(16)) multiplexer_5 (
    .in1(out_2), .in2(out_1), .in3(ins), .in4(bit_extender_1_out), .in5(bit_extender_2_out), .in6(Ins_Data),
    .out({Data, address, out_3}), .sel(S2_0));  // open: in0, in7
  or or_1 (ALU_EN, ALU_ADD, ALU_CMA, ALU_AND, X);
  or or_2 (ALU_z, ALU_ADD, ALU_CMA, ALU_AND);
  Multiplexer #(.width(16)) multiplexer_6 (.in0(out_1), .in1(out_2), .out(multiplexer_6_out), .sel(D7));
  RAM #(.addrWidth(11), .dataWidth(18), .trigger("high")) ram_1 (
    .addr(AR_Data), .we(W), .oe(R), .din(bit_extender_3_out), .dout(ram_1_dout));
  assign bit_extender_3_out = {{2{Data[15]}}, {Data, address, out_3}};  // Bit_Extender bit_extender_3
  nor nor_1 (Z, multiplexer_6_out[0], multiplexer_6_out[1], multiplexer_6_out[2], multiplexer_6_out[3], multiplexer_6_out[4], multiplexer_6_out[5], multiplexer_6_out[6], multiplexer_6_out[7], multiplexer_6_out[8], multiplexer_6_out[9], multiplexer_6_out[10], multiplexer_6_out[11], multiplexer_6_out[12], multiplexer_6_out[13], multiplexer_6_out[14], multiplexer_6_out[15]);
  assign bit_extender_4_out = {{8{1'b0}}, INP_Res};  // Bit_Extender bit_extender_4
  Multiplexer #(.width(16)) multiplexer_7 (.in0(res), .in1(bit_extender_4_out), .out(multiplexer_7_out), .sel(X));
  Bit_Extender #(.in_width(18)) bit_extender_5 (.in(ram_1_dout), .out(Ins_Data));
  Adder #(.width(16)) adder_2 (.a(out_2), .b(16'h1), .out(adder_2_out));  // open: cin, cout
  Adder #(.width(11)) adder_3 (.a(AR_Data), .b(11'h1), .out(adder_3_out));  // open: cin, cout
  Multiplexer #(.width(16)) multiplexer_8 (
    .in0({Data, address, out_3}), .in1(multiplexer_7_out), .out(multiplexer_8_out), .sel(ALU_EN));
  Button LD (.out(LD_out));
  DipSwitch dipswitch_1 (
    .sw1(dipswitch_1_sw8[7]), .sw2(dipswitch_1_sw8[6]), .sw3(dipswitch_1_sw8[5]), .sw4(dipswitch_1_sw8[4]),
    .sw5(dipswitch_1_sw8[3]), .sw6(dipswitch_1_sw8[2]), .sw7(dipswitch_1_sw8[1]), .sw8(dipswitch_1_sw8[0]));
  Multiplexer #(.width(16)) multiplexer_9 (
    .in0({Data, address, out_3}), .in1(adder_2_out), .out(multiplexer_9_out), .sel(DR_INC));
  Multiplexer #(.width(11)) multiplexer_10 (
    .in0({address, out_3}), .in1(adder_3_out), .out(multiplexer_10_out), .sel(AR_INC));
  or or_3 (or_3_out, AR_INC, AR_LD);
  Button SW (.out(SW_out));
  Register #(.width(16)) IR (.D(Ins_Data), .en(IR_LD), .clk(clk), .Q(ins));  // open: clr
  Register #(.width(16)) AC (.D(multiplexer_8_out), .en(AC_LD), .clk(clk), .Q(out_1), .clr(AC_CLR));
  Register #(.width(16)) DR (.D(multiplexer_9_out), .en(or_4_out), .clk(clk), .Q(out_2));  // open: clr
  or or_4 (or_4_out, DR_INC, DR_LD);
  Register #(.width(11)) AR (.D(multiplexer_10_out), .en(or_3_out), .clk(clk), .Q(AR_Data));  // open: clr
  Register OUTR (.D(out_3), .en(OUTR_LD), .clk(clk), .Q(out_4));  // open: clr
  Register INPR (.D(INP_Data), .en(LD_DATA), .clk(clk), .Q(INP_Res));  // open: clr
  D_Flip_Flop d_ff_1 (.D(LD_DATA), .clk(clk), .Q(FGI_FLAG), .reset(FGI_CLR));  // open: Qn, preset
  D_Flip_Flop d_ff_2 (.D(OUT_DATA), .clk(clk), .Q(FGO_FLAG), .reset(FGO_CLR));  // open: Qn, preset
  Input_Output input_output_1 (
    .LD_NUM(FGI_FLAG), .FGI(LD_out), .SWITCHES(dipswitch_1_sw8), .OUTR_IN(out_4), .OUT_LEDs(SW_out),
    .FGO(FGO_FLAG), .load(LD_DATA), .INP_Data(INP_Data), .LEDs(input_output_1_leds), .OUT_DATA(OUT_DATA));
  LED led_1 (.in(input_output_1_leds[7]));
  LED led_2 (.in(input_output_1_leds[6]));
  LED led_3 (.in(input_output_1_leds[5]));
  LED led_4 (.in(input_output_1_leds[4]));
  LED led_5 (.in(input_output_1_leds[3]));
  LED led_6 (.in(input_output_1_leds[2]));
  LED led_7 (.in(input_output_1_leds[1]));
  D_Flip_Flop d_ff_3 (.D(C_Out), .clk(clk), .Q(E_FLAG), .reset(E_CLR));  // open: Qn, preset
  LED led_8 (.in(input_output_1_leds[0]));

  // Other names for the same wires on the sheet: AC_Data[15:0] = out_1; address[7:0] = out_3;
  //   Data[10:0] = {address, out_3}; DR_Data[15:0] = out_2; FGI = FGI_FLAG; FGO = FGO_FLAG; OUTR_Data[7:0] = out_4
endmodule

module Input_Output (
  input  LD_NUM,
  input  FGI,
  input  [7:0] SWITCHES,
  input  [7:0] OUTR_IN,
  input  OUT_LEDs,
  input  FGO,
  output load,
  output [7:0] INP_Data,
  output [7:0] LEDs,
  output OUT_DATA
);

  wire not_1_out, not_2_out;

  not not_1 (not_1_out, FGI);
  assign OUT_DATA = not_2_out ? OUT_LEDs : 1'bz;  // Controlled_Buffer controlled_buffer_1
  not not_2 (not_2_out, FGO);
  assign load = not_1_out ? LD_NUM : 1'bz;  // Controlled_Buffer controlled_buffer_2
  Multiplexer #(.width(8)) multiplexer_1 (.in0(OUTR_IN), .in1({8{1'b0}}), .out(LEDs), .sel(OUT_DATA));

  assign INP_Data = SWITCHES;
endmodule

module Control_Unit (
  input  Z,
  input  FGI,
  input  FGO,
  input  [15:0] ins,
  input  CLK,
  output [2:0] S2_0,
  output AR_LD,
  output MEM_READ,
  output AR_INC,
  output X,
  output ALU_AND,
  output ALU_ADD,
  output ALU_CMA,
  output MEM_WRITE,
  output E_CLR,
  output AC_CLR,
  output PC_LD,
  output FGO_CLR,
  output FGI_CLR,
  output OUTR_LD,
  output S_CLR,
  output IR_LD,
  output DR_LD,
  output AC_LD,
  output DR_INC,
  output D7,
  output PC_INC
);

  wire and_1_out, and_8_out, and_9_out, and_10_out, and_11_out, and_13_out, and_14_out, and_15_out,
       and_18_out, and_27_out, and_28_out, and_29_out, and_30_out, D0, D1, D2, D3, D4, D5, D6, D8, D9, D10,
       D11, D12, D13, D14, D15, not_1_out, SC_CLR, T0, T2, T3, T3I, T4, T4D1, T4D5, T4D6, T4D8, T4D9, T4D10,
       T4D11, T4D13, T4D14, T5, T5D0, T5D1, T5D8, T5D9, T5D12, T6, T6D0, T6D3, T6D4, T6D7, T6D9, T7, T7D7,
       T8, T9, T10, T11, T12, T13, T14, T15, x1, x2, x3, x4, x5;
  wire [3:0] counter_1_q;

  Counter #(.max('hf), .width(4)) counter_1 (
    .clr(SC_CLR), .load(1'b0), .up(1'b1), .clk(CLK), .Q(counter_1_q));  // open: count, D, carry
  Decoder #(.select(4)) decoder_1 (
    .out0(D0), .out1(D1), .out2(D2), .out3(D3), .out4(D4), .out5(D5), .out6(D6), .out7(D7), .out8(D8),
    .out9(D9), .out10(D10), .out11(D11), .out12(D12), .out13(D13), .out14(D14), .out15(D15), .sel(ins[15:12]));  // open: en
  Decoder #(.select(4)) decoder_2 (
    .out0(T0), .out1(IR_LD), .out2(T2), .out3(T3), .out4(T4), .out5(T5), .out6(T6), .out7(T7), .out8(T8),
    .out9(T9), .out10(T10), .out11(T11), .out12(T12), .out13(T13), .out14(T14), .out15(T15), .sel(counter_1_q));  // open: en
  Priority_Encoder priority_encoder_1 (
    .in1(x1), .in2(x2), .in3(x3), .in4(x4), .in5(x5), .in6(MEM_READ), .out(S2_0));  // open: in0, in7, en_in, gs, en_out
  and and_1 (and_1_out, T3, ins[11]);
  or or_1 (AR_LD, T0, T2, and_1_out);
  and and_2 (AR_INC, T4, D9);
  and and_3 (FGI_CLR, T3, D11);
  and and_4 (ALU_AND, T5, D4);
  and and_5 (ALU_ADD, T5, D3);
  and and_6 (ALU_CMA, T3, D5);
  and and_7 (S_CLR, D15, T4);
  and and_8 (and_8_out, T4, D0);
  and and_9 (and_9_out, T4, D3);
  and and_10 (and_10_out, T4, D4);
  and and_11 (and_11_out, T4, D7);
  and and_12 (DR_INC, T5, D7);
  and and_13 (and_13_out, T6D7, Z);
  and and_14 (and_14_out, T3, FGO, D14);
  and and_15 (and_15_out, T3, FGI, D13);
  not not_1 (not_1_out, ins[11]);
  or or_2 (DR_LD, and_8_out, and_9_out, and_10_out, and_11_out);
  or or_3 (PC_INC, IR_LD, and_13_out, and_14_out, and_15_out);
  and and_16 (E_CLR, T3, D10);
  and and_17 (AC_CLR, T3, D6);
  or or_4 (x1, T6D7, T5D0);
  or or_5 (x2, T4D1, FGO_CLR);
  or or_6 (x5, T4D8, T5D9);
  or or_7 (x4, T0, T4D9);
  or or_8 (x3, T2, and_18_out);
  and and_18 (and_18_out, T4, D0, not_1_out);
  and and_19 (T4D9, T4, D9);
  and and_20 (T4D1, T4, D1);
  and and_21 (T6D7, T6, D7);
  and and_22 (T4D8, T4, D8);
  and and_23 (T5D9, T5, D9);
  and and_24 (FGO_CLR, T4, D12);
  and and_25 (T5D0, T5, D0);
  and and_26 (T3I, T3, ins[11]);
  and and_27 (and_27_out, T4, ins[11], D0);
  and and_28 (and_28_out, T4, D3);
  and and_29 (and_29_out, T4, D4);
  and and_30 (and_30_out, T4, D7);
  or or_9 (MEM_WRITE, T4D1, T6D7, T4D9);
  or or_10 (PC_LD, T4D8, T5D9);
  or or_11 (AC_LD, T5D0, ALU_ADD, ALU_AND, ALU_CMA, FGI_CLR);
  or or_12 (MEM_READ, IR_LD, T3I, and_27_out, and_28_out, and_29_out, and_30_out);
  and and_31 (T6D0, T6, D0);
  and and_32 (T5D1, T5, D1);
  and and_33 (T6D3, T6, D3);
  and and_34 (T6D4, T6, D4);
  and and_35 (T4D5, T4, D5);
  and and_36 (T4D6, T4, D6);
  and and_37 (T7D7, T7, D7);
  and and_38 (T5D8, T5, D8);
  and and_39 (T6D9, T6, D9);
  and and_40 (T4D10, T4, D10);
  and and_41 (T4D11, T4, D11);
  and and_42 (FGO_CLR, T4, D12);
  and and_43 (T5D12, T5, D12);
  and and_44 (T4D13, T4, D13);
  and and_45 (T4D14, T4, D14);
  or or_13 (SC_CLR, T6D0, T5D1, T6D3, T6D4, T4D5, T4D6, T7D7, T5D8, T6D9, T4D10, T4D11, T5D12, T4D13, T4D14);

  assign OUTR_LD = FGO_CLR;
  assign X = FGI_CLR;

  // Other names for the same wires on the sheet: I = ins[11]; opcode[3:0] = ins[15:12]; T1 = IR_LD; T3D5 = ALU_CMA;
  //   T3D6 = AC_CLR; T3D10 = E_CLR; T3D11 = FGI_CLR; T4D12 = FGO_CLR; T5D3 = ALU_ADD; T5D4 = ALU_AND; x6 = MEM_READ
endmodule
